# Fritzing sketch skematik (saved by Fritzing 0.9.3b)

parts:
  Mod1 = Raspberry Pi Pico W
  M1 = fc-51 [package=THT]
  hc-sr1 = hc-sr04

nets:
  N1: Mod1.pin_4, hc-sr1.Trig
  N2: Mod1.pin_5, hc-sr1.Echo
  N3: Mod1.pin_6, M1.pin1
  N4: Mod1.pin_36, M1.pin3
  N5: Mod1.pin_38, Mod1.pin_42, M1.pin2, hc-sr1.GND
  N6: Mod1.pin_40, hc-sr1.VCC

custom parts:
  Raspberry Pi Pico W: Raspberry Pi Pico W. Based around the RP2040 microcontroller the Pico W is a low cost microcontroller device bringing Raspberry Pi quality, cost, and easy of use to the microcontroller space. The areas marked KEEPOUT in pcb silkscreen should not have traces running through them to avoid shorts on a soldered in module!
